# Fritzing sketch io-decoder_10x10cm (saved by Fritzing 0.9.3b)
circuit board: 9.95544cm x 9.65561cm
breadboards: 1

parts:
  IC1 = IC, DIP package, 16 pins [chip_label=IC]
  J1 = female pin header, 4 pins [form="♀ (female)"]
  IC2 = IC, DIP package, 16 pins [chip_label=IC]
  J3 = female pin header, 4 pins [form="♀ (female)"]
  J4 = female pin header, 4 pins [form="♀ (female)"]
  IC3 = IC, DIP package, 16 pins [chip_label=IC]
  J2 = female pin header, 4 pins [form="♀ (female)"]
  IC4 = IC, DIP package, 16 pins [chip_label=IC]
  IC5 = IC, DIP package, 16 pins [chip_label=IC]
  J5 = female pin header, 4 pins [form="♀ (female)"]
  J6 = female pin header, 4 pins [form="♀ (female)"]
  J7 = female pin header, 4 pins [form="♀ (female)"]
  J8 = female pin header, 4 pins [form="♀ (female)"]
  J9 = female pin header, 11 pins [form="♀ (female)"]
  J10 = female pin header, 2 pins [form="♀ (female)"]
  C1 = Ceramic Capacitor [capacitance=100nF package="100 mil [THT, multilayer]"]
  J11 = female pin header, 11 pins [form="♀ (female)"]
  J12 = female pin header, 2 pins [form="♀ (female)"]
  LED1 = smd LED [color="Red (633nm)" package="1206 [SMD]"]
  R1 = Resistor [tolerance=±5% resistance=220 package="1206 [SMD]"]
  LED2 = smd LED [color="Red (633nm)" package="1206 [SMD]"]
  R2 = Resistor [tolerance=±5% resistance=220 package="1206 [SMD]"]
  LED3 = smd LED [color="Red (633nm)" package="1206 [SMD]"]
  R3 = Resistor [tolerance=±5% resistance=220 package="1206 [SMD]"]
  LED4 = smd LED [color="Red (633nm)" package="1206 [SMD]"]
  R4 = Resistor [tolerance=±5% resistance=220 package="1206 [SMD]"]
  LED5 = smd LED [color="Red (633nm)" package="1206 [SMD]"]
  R5 = Resistor [tolerance=±5% resistance=220 package="1206 [SMD]"]
  LED6 = smd LED [color="Red (633nm)" package="1206 [SMD]"]
  R6 = Resistor [tolerance=±5% resistance=220 package="1206 [SMD]"]
  LED7 = smd LED [color="Red (633nm)" package="1206 [SMD]"]
  R7 = Resistor [tolerance=±5% resistance=220 package="1206 [SMD]"]
  LED8 = smd LED [color="Red (633nm)" package="1206 [SMD]"]
  R8 = Resistor [tolerance=±5% resistance=220 package="1206 [SMD]"]
  LED9 = smd LED [color="Red (633nm)" package="1206 [SMD]"]
  R9 = Resistor [tolerance=±5% resistance=220 package="1206 [SMD]"]
  LED10 = smd LED [color="Red (633nm)" package="1206 [SMD]"]
  R10 = Resistor [tolerance=±5% resistance=220 package="1206 [SMD]"]
  LED11 = smd LED [color="Red (633nm)" package="1206 [SMD]"]
  R11 = Resistor [tolerance=±5% resistance=220 package="1206 [SMD]"]
  LED12 = smd LED [color="Red (633nm)" package="1206 [SMD]"]
  R12 = Resistor [tolerance=±5% resistance=220 package="1206 [SMD]"]
  LED13 = smd LED [color="Red (633nm)" package="1206 [SMD]"]
  R13 = Resistor [tolerance=±5% resistance=220 package="1206 [SMD]"]
  LED14 = smd LED [color="Red (633nm)" package="1206 [SMD]"]
  R14 = Resistor [tolerance=±5% resistance=220 package="1206 [SMD]"]
  LED15 = smd LED [color="Red (633nm)" package="1206 [SMD]"]
  R15 = Resistor [tolerance=±5% resistance=220 package="1206 [SMD]"]
  LED16 = smd LED [color="Red (633nm)" package="1206 [SMD]"]
  R16 = Resistor [tolerance=±5% resistance=220 package="1206 [SMD]"]
  LED17 = smd LED [color="Red (633nm)" package="1206 [SMD]"]
  R17 = Resistor [tolerance=±5% resistance=220 package="1206 [SMD]"]
  LED18 = smd LED [color="Red (633nm)" package="1206 [SMD]"]
  R18 = Resistor [tolerance=±5% resistance=220 package="1206 [SMD]"]
  LED19 = smd LED [color="Red (633nm)" package="1206 [SMD]"]
  LED20 = smd LED [color="Red (633nm)" package="1206 [SMD]"]
  R19 = Resistor [tolerance=±5% resistance=220 package="1206 [SMD]"]
  R20 = Resistor [tolerance=±5% resistance=220 package="1206 [SMD]"]
  LED21 = smd LED [color="Red (633nm)" package="1206 [SMD]"]
  LED22 = smd LED [color="Red (633nm)" package="1206 [SMD]"]
  R21 = Resistor [tolerance=±5% resistance=220 package="1206 [SMD]"]
  R22 = Resistor [tolerance=±5% resistance=220 package="1206 [SMD]"]
  LED23 = smd LED [color="Red (633nm)" package="1206 [SMD]"]
  LED24 = smd LED [color="Red (633nm)" package="1206 [SMD]"]
  R23 = Resistor [tolerance=±5% resistance=220 package="1206 [SMD]"]
  R24 = Resistor [tolerance=±5% resistance=220 package="1206 [SMD]"]
  LED25 = smd LED [color="Red (633nm)" package="1206 [SMD]"]
  LED26 = smd LED [color="Red (633nm)" package="1206 [SMD]"]
  R25 = Resistor [tolerance=±5% resistance=220 package="1206 [SMD]"]
  R26 = Resistor [tolerance=±5% resistance=220 package="1206 [SMD]"]
  LED27 = smd LED [color="Red (633nm)" package="1206 [SMD]"]
  LED28 = smd LED [color="Red (633nm)" package="1206 [SMD]"]
  R27 = Resistor [tolerance=±5% resistance=220 package="1206 [SMD]"]
  R28 = Resistor [tolerance=±5% resistance=220 package="1206 [SMD]"]
  LED29 = smd LED [color="Red (633nm)" package="1206 [SMD]"]
  LED30 = smd LED [color="Red (633nm)" package="1206 [SMD]"]
  R29 = Resistor [tolerance=±5% resistance=220 package="1206 [SMD]"]
  R30 = Resistor [tolerance=±5% resistance=220 package="1206 [SMD]"]
  LED31 = smd LED [color="Red (633nm)" package="1206 [SMD]"]
  LED32 = smd LED [color="Red (633nm)" package="1206 [SMD]"]
  R31 = Resistor [tolerance=±5% resistance=220 package="1206 [SMD]"]
  R32 = Resistor [tolerance=±5% resistance=220 package="1206 [SMD]"]
  J14 = female pin header, 12 pins [form="♀ (female)"]
  J15 = female pin header, 12 pins [form="♀ (female)"]

nets:
  N1: IC1.pin1, IC3.pin4
  N2: IC1.pin2, IC1.pin14, IC2.pin3, IC2.pin13, J15.pin4
  N3: IC1.pin3, IC1.pin13, IC2.pin2, IC2.pin14, J15.pin3
  N4: IC1.pin4, J1.pin1
  N5: IC1.pin5, J1.pin2
  N6: IC1.pin6, J1.pin3
  N7: IC1.pin7, J1.pin4
  N8: IC1.pin8, IC2.pin8, IC3.pin1, IC3.pin8, IC3.pin15, IC4.pin8, IC5.pin8, J10.pin2, C1.1, J12.pin2, J14.pin6, J14.pin8, J15.pin1
  N9: IC1.pin9, J2.pin4
  N10: IC1.pin10, J2.pin3
  N11: IC1.pin11, J2.pin2
  N12: IC1.pin12, J2.pin1
  N13: IC1.pin15, IC3.pin5
  N14: IC1.pin16, IC2.pin16, IC3.pin16, IC4.pin16, IC5.pin16, J10.pin1, C1.0, J12.pin1, R1.Pin_1, R2.Pin_1, R3.Pin_1, R4.Pin_1, R5.Pin_1, R6.Pin_1, R7.Pin_1, R8.Pin_1, R9.Pin_1, R10.Pin_1, R11.Pin_1, R12.Pin_1, R13.Pin_1, R14.Pin_1, R15.Pin_1, R16.Pin_1, R17.Pin_1, R18.Pin_1, R19.Pin_1, R20.Pin_1, R21.Pin_1, R22.Pin_1, R23.Pin_1, R24.Pin_1, R25.Pin_1, R26.Pin_1, R27.Pin_1, R28.Pin_1, R29.Pin_1, R30.Pin_1, R31.Pin_1, R32.Pin_1, J14.pin9, J14.pin12
  N15: IC2.pin1, IC3.pin6
  N16: IC2.pin4, J3.pin1
  N17: IC2.pin5, J3.pin2
  N18: IC2.pin6, J3.pin3
  N19: IC2.pin7, J3.pin4
  N20: IC2.pin9, J4.pin4
  N21: IC2.pin10, J4.pin3
  N22: IC2.pin11, J4.pin2
  N23: IC2.pin12, J4.pin1
  N24: IC2.pin15, IC3.pin7
  N25: IC3.pin2, J14.pin1
  N26: IC3.pin3, J15.pin2
  N27: IC3.pin9, IC5.pin1
  N28: IC3.pin10, IC5.pin15
  N29: IC3.pin11, IC4.pin1
  N30: IC3.pin12, IC4.pin15
  N31: IC3.pin13, J14.pin3
  N32: IC3.pin14, J14.pin2
  N33: IC4.pin2, IC4.pin14, IC5.pin3, IC5.pin13, J14.pin4
  N34: IC4.pin3, IC4.pin13, IC5.pin2, IC5.pin14, J14.pin5
  N35: IC4.pin4, J5.pin1
  N36: IC4.pin5, J5.pin2
  N37: IC4.pin6, J5.pin3
  N38: IC4.pin7, J5.pin4
  N39: IC4.pin9, J8.pin4
  N40: IC4.pin10, J8.pin3
  N41: IC4.pin11, J8.pin2
  N42: IC4.pin12, J8.pin1
  N43: IC5.pin4, J7.pin1
  N44: IC5.pin5, J7.pin2
  N45: IC5.pin6, J7.pin3
  N46: IC5.pin7, J7.pin4
  N47: IC5.pin9, J6.pin4
  N48: IC5.pin10, J6.pin3
  N49: IC5.pin11, J6.pin2
  N50: IC5.pin12, J6.pin1
  N51: J9.pin1, J11.pin1, J15.pin5
  N52: J9.pin2, J11.pin2, J15.pin6
  N53: J9.pin3, J11.pin3, J15.pin7
  N54: J9.pin4, J11.pin4, J15.pin8
  N55: J9.pin5, J11.pin5, J15.pin9
  N56: J9.pin6, J11.pin6, J15.pin10
  N57: J9.pin7, J11.pin7, J15.pin11
  N58: J9.pin8, J11.pin8, J15.pin12
  N59: J9.pin9, J11.pin9, J14.pin11
  N60: J9.pin10, J11.pin10, J14.pin10
  N61: J9.pin11, J11.pin11, J14.pin7
  N62: LED1.anode, R1.Pin_0
  N63: LED2.anode, R2.Pin_0
  N64: LED3.anode, R3.Pin_0
  N65: LED4.anode, R4.Pin_0
  N66: LED5.anode, R5.Pin_0
  N67: LED6.anode, R6.Pin_0
  N68: LED7.anode, R7.Pin_0
  N69: LED8.anode, R8.Pin_0
  N70: LED9.anode, R9.Pin_0
  N71: LED10.anode, R10.Pin_0
  N72: LED11.anode, R11.Pin_0
  N73: LED12.anode, R12.Pin_0
  N74: LED13.anode, R13.Pin_0
  N75: LED14.anode, R14.Pin_0
  N76: LED15.anode, R15.Pin_0
  N77: LED16.anode, R16.Pin_0
  N78: LED17.anode, R17.Pin_0
  N79: LED18.anode, R18.Pin_0
  N80: LED19.anode, R19.Pin_0
  N81: LED20.anode, R20.Pin_0
  N82: LED21.anode, R22.Pin_0
  N83: LED22.anode, R21.Pin_0
  N84: LED23.anode, R23.Pin_0
  N85: LED24.anode, R24.Pin_0
  N86: LED25.anode, R25.Pin_0
  N87: LED26.anode, R26.Pin_0
  N88: LED27.anode, R28.Pin_0
  N89: LED28.anode, R27.Pin_0
  N90: LED29.anode, R30.Pin_0
  N91: LED30.anode, R29.Pin_0
  N92: LED31.anode, R31.Pin_0
  N93: LED32.anode, R32.Pin_0
