# Fritzing sketch MAR_v2 (saved by Fritzing 0.9.1b)
circuit board: 9.99058cm x 9.99059cm
breadboards: 2

parts:
  C6 = Ceramic Capacitor [capacitance=100nF package="100 mil [THT, multilayer]"]
  74LS161_B-HIGH1 = IC, DIP package, 16 pins [chip_label=IC]
  74LS161_B-LOW1 = IC, DIP package, 16 pins [chip_label=IC]
  74LS161_A-LOW1 = IC, DIP package, 16 pins [chip_label=IC]
  74LS161_A-HIGH1 = IC, DIP package, 16 pins [chip_label=IC]
  CNT = female pin header, 1 pin [form="♀ (female)"]
  LOAD-H = female pin header, 1 pin [form="♀ (female)"]
  CLK = female pin header, 1 pin [form="♀ (female)"]
  + = female pin header, 1 pin [form="♀ (female)"]
  - = female pin header, 1 pin [form="♀ (female)"]
  J38 = female pin header, 2 pins [form="♀ (female)"]
  J39 = female pin header, 8 pins [form="♀ (female)"]
  330 = Resistor [tolerance=±5% resistance=330 package="1206 [SMD]"]
  J40 = female pin header, 1 pin [form="♀ (female)"]
  J41 = female pin header, 1 pin [form="♀ (female)"]
  J42 = female pin header, 2 pins [form="♀ (female)"]
  C7 = Ceramic Capacitor [capacitance=100nF package="100 mil [THT, multilayer]"]
  J43 = female pin header, 8 pins [form="♀ (female)"]
  LOAD-L = female pin header, 1 pin [form="♀ (female)"]
  74LS173 = IC, DIP package, 16 pins [chip_label=IC]
  74LS173_2 = IC, DIP package, 16 pins [chip_label=IC]
  J44 = female pin header, 8 pins [form="♀ (female)"]
  74LS283 = IC, DIP package, 16 pins [chip_label=IC]
  ADDR = female pin header, 8 pins [form="♀ (female)"]  # not connected
  ADDR1 = female pin header, 8 pins [form="♀ (female)"]
  74LS283_2 = IC, DIP package, 16 pins [chip_label=IC]
  74LS285 = IC, DIP package, 16 pins [chip_label=IC]
  74LS286 = IC, DIP package, 16 pins [chip_label=IC]
  ADDR2 = female pin header, 8 pins [form="♀ (female)"]  # not connected
  ADDR3 = female pin header, 8 pins [form="♀ (female)"]  # not connected
  C8 = Ceramic Capacitor [capacitance=100nF package="100 mil [THT, multilayer]"]
  C9 = Ceramic Capacitor [capacitance=100nF package="100 mil [THT, multilayer]"]

nets:
  N1: C6.0, 74LS161_B-HIGH1.pin1, 74LS161_B-HIGH1.pin16, 74LS161_B-LOW1.pin1, 74LS161_B-LOW1.pin16, 74LS161_A-LOW1.pin1, 74LS161_A-LOW1.pin16, 74LS161_A-HIGH1.pin1, 74LS161_A-HIGH1.pin16, +.pin1, J38.pin2, J40.pin1, J42.pin2, C7.0, 74LS173.pin16, 74LS173_2.pin16, C8.1, C9.1
  N2: C6.1, 74LS161_B-HIGH1.pin8, 74LS161_B-LOW1.pin8, 74LS161_A-LOW1.pin8, 74LS161_A-HIGH1.pin8, -.pin1, J38.pin1, J41.pin1, J42.pin1, C7.1
  N3: 74LS161_B-HIGH1.pin2, 74LS161_B-LOW1.pin2, 74LS161_A-LOW1.pin2, 74LS161_A-HIGH1.pin2, 330.Pin_1, 74LS173.pin7, 74LS173_2.pin7
  N4: 74LS161_B-HIGH1.pin3, J43.pin4
  N5: 74LS161_B-HIGH1.pin4, J43.pin3
  N6: 74LS161_B-HIGH1.pin5, J43.pin2
  N7: 74LS161_B-HIGH1.pin6, J43.pin1
  N8: 74LS161_B-HIGH1.pin7, 74LS161_B-HIGH1.pin10, 74LS161_B-LOW1.pin15
  N9: 74LS161_B-HIGH1.pin9, 74LS161_B-LOW1.pin9, LOAD-L.pin1
  N10: 74LS161_B-HIGH1.pin11, 74LS283_2.pin11
  N11: 74LS161_B-HIGH1.pin12, 74LS283_2.pin15
  N12: 74LS161_B-HIGH1.pin13, 74LS283_2.pin2
  N13: 74LS161_B-HIGH1.pin14, 74LS283_2.pin6
  N14: 74LS161_B-HIGH1.pin15, 74LS161_A-LOW1.pin7, 74LS161_A-LOW1.pin10
  N15: 74LS161_B-LOW1.pin3, J43.pin8
  N16: 74LS161_B-LOW1.pin4, J43.pin7
  N17: 74LS161_B-LOW1.pin5, J43.pin6
  N18: 74LS161_B-LOW1.pin6, J43.pin5
  N19: 74LS161_B-LOW1.pin7, 74LS161_B-LOW1.pin10, CNT.pin1
  N20: 74LS161_B-LOW1.pin11, 74LS283.pin11
  N21: 74LS161_B-LOW1.pin12, 74LS283.pin15
  N22: 74LS161_B-LOW1.pin13, 74LS283.pin2
  N23: 74LS161_B-LOW1.pin14, 74LS283.pin6
  N24: 74LS161_A-LOW1.pin3, J39.pin8
  N25: 74LS161_A-LOW1.pin4, J39.pin7
  N26: 74LS161_A-LOW1.pin5, J39.pin6
  N27: 74LS161_A-LOW1.pin6, J39.pin5
  N28: 74LS161_A-LOW1.pin9, 74LS161_A-HIGH1.pin9, LOAD-H.pin1
  N29: 74LS161_A-LOW1.pin15, 74LS161_A-HIGH1.pin7, 74LS161_A-HIGH1.pin10
  N30: 74LS161_A-HIGH1.pin3, J39.pin4
  N31: 74LS161_A-HIGH1.pin4, J39.pin3
  N32: 74LS161_A-HIGH1.pin5, J39.pin2
  N33: 74LS161_A-HIGH1.pin6, J39.pin1
  N34: CLK.pin1, 330.Pin_0
  N35: 74LS173.pin1, 74LS173.pin2, 74LS173.pin8, 74LS173.pin15, 74LS173_2.pin1, 74LS173_2.pin2, 74LS173_2.pin8, 74LS173_2.pin15, 74LS283.pin7, 74LS283.pin8, 74LS283_2.pin8, 74LS285.pin8, 74LS286.pin8, C8.0, C9.0
  N36: 74LS173.pin3, 74LS283_2.pin12
  N37: 74LS173.pin4, 74LS283_2.pin14
  N38: 74LS173.pin5, 74LS283_2.pin3
  N39: 74LS173.pin6, 74LS283_2.pin5
  N40: 74LS173.pin9, 74LS173.pin10, 74LS173_2.pin9, 74LS173_2.pin10
  N41: 74LS173.pin11, J44.pin4
  N42: 74LS173.pin12, J44.pin3
  N43: 74LS173.pin13, J44.pin2
  N44: 74LS173.pin14, J44.pin1
  N45: 74LS173_2.pin3, 74LS283.pin12
  N46: 74LS173_2.pin4, 74LS283.pin14
  N47: 74LS173_2.pin5, 74LS283.pin3
  N48: 74LS173_2.pin6, 74LS283.pin5
  N49: 74LS173_2.pin11, J44.pin8
  N50: 74LS173_2.pin12, J44.pin7
  N51: 74LS173_2.pin13, J44.pin6
  N52: 74LS173_2.pin14, J44.pin5
  N53: 74LS283.pin1, ADDR1.pin7
  N54: 74LS283.pin4, ADDR1.pin8
  N55: 74LS283.pin9, 74LS283_2.pin7
  N56: 74LS283.pin10, ADDR1.pin5
  N57: 74LS283.pin13, ADDR1.pin6
  N58: 74LS283.pin16, 74LS283_2.pin16
  N59: ADDR1.pin1, 74LS283_2.pin10
  N60: ADDR1.pin2, 74LS283_2.pin13
  N61: ADDR1.pin3, 74LS283_2.pin1
  N62: ADDR1.pin4, 74LS283_2.pin4
  N63: 74LS283_2.pin9, 74LS286.pin7
  N64: 74LS285.pin7, 74LS286.pin9
