# Fritzing sketch PC_display_v2 (saved by Fritzing 0.9.1b)
circuit board: 9.99cm x 9.99cm
breadboards: 1

parts:
  J39 = female pin header, 8 pins [form="♀ (female)"]  # not connected
  J40 = female pin header, 8 pins [form="♀ (female)"]  # not connected
  J41 = female pin header, 4 pins [form="♀ (female)"]
  J42 = female pin header, 4 pins [form="♀ (female)"]
  J43 = female pin header, 4 pins [form="♀ (female)"]
  J44 = female pin header, 4 pins [form="♀ (female)"]
  GND5 = female pin header, 4 pins [form="♀ (female)"]  # not connected
  VCC1 = female pin header, 4 pins [form="♀ (female)"]  # not connected
  flags1 = female pin header, 4 pins [form="♀ (female)"]  # not connected
  jmp_cond1 = female pin header, 4 pins [form="♀ (female)"]  # not connected
  555 = 555 Timer [package="DIP8 [THT]"]
  74LS163 = IC, DIP package, 16 pins [chip_label=IC]
  R1 = Resistor [tolerance=±5% resistance=220 package=THT]
  R2 = Resistor [tolerance=±5% resistance=220 package=THT]
  C1 = Ceramic Capacitor [capacitance=100nF package="100 mil [THT, multilayer]"]
  74LS139 = IC, DIP package, 16 pins [chip_label=IC]
  COM = female pin header, 4 pins [form="♀ (female)"]
  C2 = Ceramic Capacitor [capacitance=100nF package="100 mil [THT, multilayer]"]
  display-1 = female pin header, 6 pins [form="♀ (female)"]  # not connected
  display-2 = female pin header, 6 pins [form="♀ (female)"]  # not connected
  74LS157 = IC, DIP package, 16 pins [chip_label=IC]
  74LS164 = IC, DIP package, 16 pins [chip_label=IC]
  J45 = female pin header, 12 pins [form="♀ (female)"]
  J46 = female pin header, 12 pins [form="♀ (female)"]

nets:
  N1: J41.pin1, 74LS164.pin10
  N2: J41.pin2, 74LS164.pin13
  N3: J41.pin3, 74LS164.pin6
  N4: J41.pin4, 74LS164.pin3
  N5: J42.pin1, 74LS157.pin10
  N6: J42.pin2, 74LS157.pin13
  N7: J42.pin3, 74LS157.pin6
  N8: J42.pin4, 74LS157.pin3
  N9: J43.pin1, 74LS164.pin11
  N10: J43.pin2, 74LS164.pin14
  N11: J43.pin3, 74LS164.pin5
  N12: J43.pin4, 74LS164.pin2
  N13: J44.pin1, 74LS157.pin11
  N14: J44.pin2, 74LS157.pin14
  N15: J44.pin3, 74LS157.pin5
  N16: J44.pin4, 74LS157.pin2
  N17: 555.Ground, 74LS163.pin8, C1.1, 74LS139.pin1, 74LS139.pin8, C2.0, 74LS157.pin8, 74LS157.pin15, 74LS164.pin8, 74LS164.pin15, J45.pin12
  N18: 555.Trigger, 555.Threshold, R2.Pin_0, C1.0
  N19: 555.Output, 74LS163.pin2
  N20: 555.Discharge, R1.Pin_0, R2.Pin_1
  N21: 555.Vcc_Supply_Voltage, 74LS163.pin1, 74LS163.pin7, 74LS163.pin9, 74LS163.pin10, 74LS163.pin16, R1.Pin_1, 74LS139.pin16, C2.1, 74LS157.pin16, 74LS164.pin16, J46.pin1
  N22: 74LS163.pin13, 74LS139.pin3, 74LS157.pin1, 74LS164.pin1
  N23: 74LS163.pin14, 74LS139.pin2
  N24: 74LS139.pin4, COM.pin1
  N25: 74LS139.pin5, COM.pin2
  N26: 74LS139.pin6, COM.pin3
  N27: 74LS139.pin7, COM.pin4
  N28: 74LS157.pin4, J45.pin4
  N29: 74LS157.pin7, J45.pin3
  N30: 74LS157.pin9, J45.pin1
  N31: 74LS157.pin12, J45.pin2
  N32: 74LS164.pin4, J45.pin8
  N33: 74LS164.pin7, J45.pin7
  N34: 74LS164.pin9, J45.pin5
  N35: 74LS164.pin12, J45.pin6
