# Fritzing sketch PC_v2 (saved by Fritzing 0.9.1b)
circuit board: 9.99cm x 9.99cm
breadboards: 1

parts:
  74LS173-1 = IC, DIP package, 16 pins [chip_label=IC]
  74LS173-2 = IC, DIP package, 16 pins [chip_label=IC]
  J28 = female pin header, 8 pins [form="♀ (female)"]
  74LS161-1 = IC, DIP package, 16 pins [chip_label=IC]
  74LS161-2 = IC, DIP package, 16 pins [chip_label=IC]
  74LS173-3 = IC, DIP package, 16 pins [chip_label=IC]
  74LS173-4 = IC, DIP package, 16 pins [chip_label=IC]
  74LS161-3 = IC, DIP package, 16 pins [chip_label=IC]
  74LS161-4 = IC, DIP package, 16 pins [chip_label=IC]
  C11 = Ceramic Capacitor [capacitance=100nF package="100 mil [THT, multilayer]"]
  C12 = Ceramic Capacitor [capacitance=100nF package="100 mil [THT, multilayer]"]
  C13 = Ceramic Capacitor [capacitance=100nF package="100 mil [THT, multilayer]"]
  C14 = Ceramic Capacitor [capacitance=100nF package="100 mil [THT, multilayer]"]
  LOAD-HIGH = female pin header, 1 pin [form="♀ (female)"]
  LOAD-LOW = female pin header, 1 pin [form="♀ (female)"]
  CLK = female pin header, 1 pin [form="♀ (female)"]
  C15 = Ceramic Capacitor [capacitance=100nF package="100 mil [THT, multilayer]"]
  C16 = Ceramic Capacitor [capacitance=100nF package="100 mil [THT, multilayer]"]
  C17 = Ceramic Capacitor [capacitance=100nF package="100 mil [THT, multilayer]"]
  C18 = Ceramic Capacitor [capacitance=100nF package="100 mil [THT, multilayer]"]
  flags4 = female pin header, 12 pins [form="♀ (female)"]
  flags5 = female pin header, 12 pins [form="♀ (female)"]
  J33 = female pin header, 4 pins [form="♀ (female)"]
  J34 = female pin header, 4 pins [form="♀ (female)"]
  J35 = female pin header, 4 pins [form="♀ (female)"]
  J36 = female pin header, 4 pins [form="♀ (female)"]
  RESET = female pin header, 1 pin [form="♀ (female)"]
  CNT = female pin header, 1 pin [form="♀ (female)"]
  jmp_cond = female pin header, 4 pins [form="♀ (female)"]
  flags = female pin header, 4 pins [form="♀ (female)"]
  jmp_cond1 = female pin header, 4 pins [form="♀ (female)"]
  J37 = female pin header, 8 pins [form="♀ (female)"]
  J38 = female pin header, 8 pins [form="♀ (female)"]
  J39 = female pin header, 8 pins [form="♀ (female)"]
  J40 = female pin header, 8 pins [form="♀ (female)"]
  flags6 = female pin header, 4 pins [form="♀ (female)"]
  GND4 = female pin header, 4 pins [form="♀ (female)"]
  VCC4 = female pin header, 4 pins [form="♀ (female)"]
  VCC = female pin header, 4 pins [form="♀ (female)"]
  GND = female pin header, 4 pins [form="♀ (female)"]
  J51 = female pin header, 1 pin [form="♀ (female)"]
  J52 = female pin header, 4 pins [form="♀ (female)"]

nets:
  N1: 74LS173-1.pin1, 74LS173-1.pin2, 74LS173-1.pin8, 74LS173-1.pin15, 74LS173-2.pin1, 74LS173-2.pin2, 74LS173-2.pin8, 74LS173-2.pin15, 74LS161-1.pin8, 74LS161-2.pin8, 74LS173-3.pin1, 74LS173-3.pin2, 74LS173-3.pin8, 74LS173-3.pin15, 74LS173-4.pin1, 74LS173-4.pin2, 74LS173-4.pin8, 74LS173-4.pin15, 74LS161-3.pin8, 74LS161-4.pin8, C11.0, C12.0, C13.0, C14.0, C15.1, C16.1, C17.1, C18.1, flags4.pin6, flags4.pin7, flags4.pin8, flags4.pin10, flags4.pin11, flags5.pin1, GND4.pin1, GND4.pin2, GND4.pin3, GND4.pin4, GND.pin1, GND.pin2, GND.pin3, GND.pin4, J52.pin1, J52.pin2
  N2: 74LS173-1.pin3, 74LS161-1.pin6, J33.pin1
  N3: 74LS173-1.pin4, 74LS161-1.pin5, J33.pin2
  N4: 74LS173-1.pin5, 74LS161-1.pin4, J33.pin3
  N5: 74LS173-1.pin6, 74LS161-1.pin3, J33.pin4
  N6: 74LS173-1.pin7, 74LS173-2.pin7, 74LS161-1.pin2, 74LS161-2.pin2, 74LS173-3.pin7, 74LS173-4.pin7, 74LS161-3.pin2, 74LS161-4.pin2, CLK.pin1
  N7: 74LS173-1.pin9, 74LS173-1.pin10, 74LS173-2.pin9, 74LS173-2.pin10, LOAD-HIGH.pin1
  N8: 74LS173-1.pin11, J28.pin4, 74LS173-4.pin11
  N9: 74LS173-1.pin12, J28.pin3, 74LS173-4.pin12
  N10: 74LS173-1.pin13, J28.pin2, 74LS173-4.pin13
  N11: 74LS173-1.pin14, J28.pin1, 74LS173-4.pin14
  N12: 74LS173-1.pin16, 74LS173-2.pin16, 74LS161-1.pin16, 74LS161-2.pin16, 74LS173-3.pin16, 74LS173-4.pin16, 74LS161-3.pin16, 74LS161-4.pin16, C11.1, C12.1, C13.1, C14.1, C15.0, C16.0, C17.0, C18.0, flags4.pin9, flags4.pin12, VCC4.pin1, VCC4.pin2, VCC4.pin3, VCC4.pin4, VCC.pin1, VCC.pin2, VCC.pin3, VCC.pin4, J52.pin3, J52.pin4
  N13: 74LS173-2.pin3, 74LS161-2.pin6, J34.pin1
  N14: 74LS173-2.pin4, 74LS161-2.pin5, J34.pin2
  N15: 74LS173-2.pin5, 74LS161-2.pin4, J34.pin3
  N16: 74LS173-2.pin6, 74LS161-2.pin3, J34.pin4
  N17: 74LS173-2.pin11, J28.pin8, 74LS173-3.pin11
  N18: 74LS173-2.pin12, J28.pin7, 74LS173-3.pin12
  N19: 74LS173-2.pin13, J28.pin6, 74LS173-3.pin13
  N20: 74LS173-2.pin14, J28.pin5, 74LS173-3.pin14
  N21: 74LS161-1.pin1, 74LS161-2.pin1, 74LS161-3.pin1, 74LS161-4.pin1, RESET.pin1
  N22: 74LS161-1.pin7, 74LS161-1.pin10, 74LS161-2.pin15
  N23: 74LS161-1.pin9, 74LS161-2.pin9, 74LS161-3.pin9, 74LS161-4.pin9, flags5.pin4, J51.pin1
  N24: 74LS161-1.pin11, J37.pin1, J39.pin1
  N25: 74LS161-1.pin12, J37.pin2, J39.pin2
  N26: 74LS161-1.pin13, J37.pin3, J39.pin3
  N27: 74LS161-1.pin14, J37.pin4, J39.pin4
  N28: 74LS161-2.pin7, 74LS161-2.pin10, 74LS161-3.pin15
  N29: 74LS161-2.pin11, J37.pin5, J39.pin5
  N30: 74LS161-2.pin12, J37.pin6, J39.pin6
  N31: 74LS161-2.pin13, J37.pin7, J39.pin7
  N32: 74LS161-2.pin14, J37.pin8, J39.pin8
  N33: 74LS173-3.pin3, 74LS161-4.pin6, J36.pin1
  N34: 74LS173-3.pin4, 74LS161-4.pin5, J36.pin2
  N35: 74LS173-3.pin5, 74LS161-4.pin4, J36.pin3
  N36: 74LS173-3.pin6, 74LS161-4.pin3, J36.pin4
  N37: 74LS173-3.pin9, 74LS173-3.pin10, 74LS173-4.pin9, 74LS173-4.pin10, LOAD-LOW.pin1
  N38: 74LS173-4.pin3, 74LS161-3.pin6, J35.pin1
  N39: 74LS173-4.pin4, 74LS161-3.pin5, J35.pin2
  N40: 74LS173-4.pin5, 74LS161-3.pin4, J35.pin3
  N41: 74LS173-4.pin6, 74LS161-3.pin3, J35.pin4
  N42: 74LS161-3.pin7, 74LS161-3.pin10, 74LS161-4.pin15
  N43: 74LS161-3.pin11, J38.pin1, J40.pin1
  N44: 74LS161-3.pin12, J38.pin2, J40.pin2
  N45: 74LS161-3.pin13, J38.pin3, J40.pin3
  N46: 74LS161-3.pin14, J38.pin4, J40.pin4
  N47: 74LS161-4.pin7, 74LS161-4.pin10, CNT.pin1
  N48: 74LS161-4.pin11, J38.pin5, J40.pin5
  N49: 74LS161-4.pin12, J38.pin6, J40.pin6
  N50: 74LS161-4.pin13, J38.pin7, J40.pin7
  N51: 74LS161-4.pin14, J38.pin8, J40.pin8
  N52: flags5.pin5, jmp_cond.pin4, jmp_cond1.pin4
  N53: flags5.pin6, jmp_cond.pin3, jmp_cond1.pin3
  N54: flags5.pin7, jmp_cond.pin2, jmp_cond1.pin2
  N55: flags5.pin8, jmp_cond.pin1, jmp_cond1.pin1
  N56: flags5.pin9, flags.pin1, flags6.pin1
  N57: flags5.pin10, flags.pin2, flags6.pin2
  N58: flags5.pin11, flags.pin3, flags6.pin3
  N59: flags5.pin12, flags.pin4, flags6.pin4

notes:
  PROGRAM COUNTER
  Marius Krabset 2019
  -
  +
  #0
  c
  n
  z
  v
  #1
  #2
  #3
