# Fritzing sketch RAM_v2 (saved by Fritzing 0.9.1b)
circuit board: 9.99058cm x 9.99059cm
circuit board: 12.3934cm x 9.06819cm
circuit board: 9.99058cm x 9.99059cm
breadboards: 2

parts:
  power = female pin header, 2 pins [form="♀ (female)"]
  bus = female pin header, 8 pins [form="♀ (female)"]
  74245 = IC, DIP package, 20 pins [chip_label=IC]
  74LS173-H = IC, DIP package, 16 pins [chip_label=IC]
  74LS173-L = IC, DIP package, 16 pins [chip_label=IC]
  IS61C256AH = IC, DIP package, 28 pins [chip_label=IC]
  J27 = female pin header, 15 pins [form="♀ (female)"]
  C1 = Ceramic Capacitor [capacitance=100nF package="100 mil [THT, multilayer]"]
  bus-to-ram_(active_low) = female pin header, 1 pin [form="♀ (female)"]
  ram-to-bus_(active_low) = female pin header, 1 pin [form="♀ (female)"]
  CLK = female pin header, 1 pin [form="♀ (female)"]
  74LS74 = IC, DIP package, 14 pins [chip_label=IC]
  C2 = Ceramic Capacitor [capacitance=100nF package="100 mil [THT, multilayer]"]
  C3 = Ceramic Capacitor [capacitance=100nF package="100 mil [THT, multilayer]"]
  J28 = female pin header, 2 pins [form="♀ (female)"]
  C4 = Ceramic Capacitor [capacitance=100nF package="100 mil [THT, multilayer]"]
  GND2 = female pin header, 4 pins [form="♀ (female)"]
  VCC2 = female pin header, 4 pins [form="♀ (female)"]
  GND3 = female pin header, 4 pins [form="♀ (female)"]
  VCC3 = female pin header, 4 pins [form="♀ (female)"]
  ADDR4 = female pin header, 8 pins [form="♀ (female)"]
  ADDR5 = female pin header, 8 pins [form="♀ (female)"]
  ADDR6 = female pin header, 8 pins [form="♀ (female)"]
  ADDR7 = female pin header, 8 pins [form="♀ (female)"]
  GND = female pin header, 4 pins [form="♀ (female)"]  # not connected
  VCC4 = female pin header, 4 pins [form="♀ (female)"]  # not connected
  ADDR8 = female pin header, 8 pins [form="♀ (female)"]
  ADDR9 = female pin header, 8 pins [form="♀ (female)"]  # not connected
  74245_2 = IC, DIP package, 20 pins [chip_label=IC]
  74LS173-H1 = IC, DIP package, 16 pins [chip_label=IC]
  74LS173-L1 = IC, DIP package, 16 pins [chip_label=IC]
  bus1 = female pin header, 8 pins [form="♀ (female)"]
  C5 = Ceramic Capacitor [capacitance=100nF package="100 mil [THT, multilayer]"]
  IS61C256AH1 = IC, DIP package, 32 pins [chip_label=IC]

nets:
  N1: power.pin1, 74245.pin1, 74245.pin20, 74LS173-H.pin16, 74LS173-L.pin16, IS61C256AH.pin28, C1.1, 74LS74.pin1, 74LS74.pin10, 74LS74.pin13, 74LS74.pin14, C2.1, C3.0, J28.pin1, C4.0
  N2: power.pin2, 74245.pin10, 74LS173-H.pin8, 74LS173-H.pin15, 74LS173-L.pin8, 74LS173-L.pin15, IS61C256AH.pin14, IS61C256AH.pin20, C1.0, 74LS74.pin7, C2.0, C3.1, J28.pin2, C4.1
  N3: bus.pin1, 74245.pin18, 74LS173-H.pin14
  N4: bus.pin2, 74245.pin17, 74LS173-H.pin13
  N5: bus.pin3, 74245.pin16, 74LS173-H.pin12
  N6: bus.pin4, 74245.pin15, 74LS173-H.pin11
  N7: bus.pin5, 74245.pin14, 74LS173-L.pin14
  N8: bus.pin6, 74245.pin13, 74LS173-L.pin13
  N9: bus.pin7, 74245.pin12, 74LS173-L.pin12
  N10: bus.pin8, 74245.pin11, 74LS173-L.pin11
  N11: 74245.pin2, 74LS173-H.pin3, IS61C256AH.pin19
  N12: 74245.pin3, 74LS173-H.pin4, IS61C256AH.pin18
  N13: 74245.pin4, 74LS173-H.pin5, IS61C256AH.pin17
  N14: 74245.pin5, 74LS173-H.pin6, IS61C256AH.pin16
  N15: 74245.pin6, 74LS173-L.pin3, IS61C256AH.pin15
  N16: 74245.pin7, 74LS173-L.pin4, IS61C256AH.pin13
  N17: 74245.pin8, 74LS173-L.pin5, IS61C256AH.pin12
  N18: 74245.pin9, 74LS173-L.pin6, IS61C256AH.pin11
  N19: 74245.pin19, IS61C256AH.pin22, ram-to-bus_(active_low).pin1
  N20: 74LS173-H.pin1, 74LS173-H.pin2, 74LS173-L.pin1, 74LS173-L.pin2, 74LS74.pin9
  N21: 74LS173-H.pin7, 74LS173-L.pin7, CLK.pin1, 74LS74.pin3, 74LS74.pin4, 74LS74.pin11
  N22: 74LS173-H.pin9, 74LS173-H.pin10, 74LS173-L.pin9, 74LS173-L.pin10, bus-to-ram_(active_low).pin1, 74LS74.pin2, 74LS74.pin12
  N23: IS61C256AH.pin1, J27.pin1
  N24: IS61C256AH.pin2, J27.pin3
  N25: IS61C256AH.pin3, J27.pin8
  N26: IS61C256AH.pin4, J27.pin9
  N27: IS61C256AH.pin5, J27.pin10
  N28: IS61C256AH.pin6, J27.pin11
  N29: IS61C256AH.pin7, J27.pin12
  N30: IS61C256AH.pin8, J27.pin13
  N31: IS61C256AH.pin9, J27.pin14
  N32: IS61C256AH.pin10, J27.pin15
  N33: IS61C256AH.pin21, J27.pin5
  N34: IS61C256AH.pin23, J27.pin4
  N35: IS61C256AH.pin24, J27.pin6
  N36: IS61C256AH.pin25, J27.pin7
  N37: IS61C256AH.pin26, J27.pin2
  N38: IS61C256AH.pin27, 74LS74.pin5
  N39: GND2.pin1, GND2.pin2, GND2.pin3, GND2.pin4, GND3.pin1, GND3.pin2, GND3.pin3, GND3.pin4
  N40: VCC2.pin1, VCC2.pin2, VCC2.pin3, VCC2.pin4, VCC3.pin1, VCC3.pin2, VCC3.pin3, VCC3.pin4
  N41: ADDR4.pin1, ADDR6.pin1
  N42: ADDR4.pin2, ADDR6.pin2
  N43: ADDR4.pin3, ADDR6.pin3
  N44: ADDR4.pin4, ADDR6.pin4
  N45: ADDR4.pin5, ADDR6.pin5
  N46: ADDR4.pin6, ADDR6.pin6
  N47: ADDR4.pin7, ADDR6.pin7
  N48: ADDR4.pin8, ADDR6.pin8
  N49: ADDR5.pin1, ADDR7.pin1
  N50: ADDR5.pin2, ADDR7.pin2
  N51: ADDR5.pin3, ADDR7.pin3
  N52: ADDR5.pin4, ADDR7.pin4
  N53: ADDR5.pin5, ADDR7.pin5
  N54: ADDR5.pin6, ADDR7.pin6
  N55: ADDR5.pin7, ADDR7.pin7
  N56: ADDR5.pin8, ADDR7.pin8
  N57: ADDR8.pin5, IS61C256AH1.pin9
  N58: ADDR8.pin6, IS61C256AH1.pin10
  N59: ADDR8.pin7, IS61C256AH1.pin11
  N60: ADDR8.pin8, IS61C256AH1.pin12
  N61: 74245_2.pin1, 74245_2.pin20, C5.0
  N62: 74245_2.pin2, 74LS173-H1.pin3, IS61C256AH1.pin21
  N63: 74245_2.pin3, 74LS173-H1.pin4, IS61C256AH1.pin20
  N64: 74245_2.pin4, 74LS173-H1.pin5, IS61C256AH1.pin19
  N65: 74245_2.pin5, 74LS173-H1.pin6, IS61C256AH1.pin18
  N66: 74245_2.pin6, 74LS173-L1.pin3, IS61C256AH1.pin17
  N67: 74245_2.pin7, 74LS173-L1.pin4, IS61C256AH1.pin15
  N68: 74245_2.pin8, 74LS173-L1.pin5, IS61C256AH1.pin14
  N69: 74245_2.pin9, 74LS173-L1.pin6, IS61C256AH1.pin13
  N70: 74245_2.pin10, C5.1
  N71: 74245_2.pin11, 74LS173-L1.pin11, bus1.pin8
  N72: 74245_2.pin12, 74LS173-L1.pin12, bus1.pin7
  N73: 74245_2.pin13, 74LS173-L1.pin13, bus1.pin6
  N74: 74245_2.pin14, 74LS173-L1.pin14, bus1.pin5
  N75: 74245_2.pin15, 74LS173-H1.pin11, bus1.pin4
  N76: 74245_2.pin16, 74LS173-H1.pin12, bus1.pin3
  N77: 74245_2.pin17, 74LS173-H1.pin13, bus1.pin2
  N78: 74245_2.pin18, 74LS173-H1.pin14, bus1.pin1
