# Fritzing sketch xtal-clock (saved by Fritzing 0.9.1b)
circuit board: 12.0465cm x 4.89464cm
breadboards: 1

parts:
  XTAL = female pin header, 1 pin [form="♀ (female)"]
  RESET = female pin header, 1 pin [form="♀ (female)"]
  74ls161-0 = IC, DIP package, 16 pins [chip_label=IC]
  74ls161-1 = IC, DIP package, 16 pins [chip_label=IC]
  74ls161-2 = IC, DIP package, 16 pins [chip_label=IC]
  74ls161-3 = IC, DIP package, 16 pins [chip_label=IC]
  74ls161-4 = IC, DIP package, 16 pins [chip_label=IC]
  J1 = female pin header, 4 pins [form="♀ (female)"]
  J2 = female pin header, 4 pins [form="♀ (female)"]
  J3 = female pin header, 4 pins [form="♀ (female)"]
  J4 = female pin header, 4 pins [form="♀ (female)"]
  J5 = female pin header, 4 pins [form="♀ (female)"]
  J6 = female pin header, 4 pins [form="♀ (female)"]

nets:
  N1: XTAL.pin1, 74ls161-0.pin2, 74ls161-1.pin2, 74ls161-2.pin2, 74ls161-3.pin2, 74ls161-4.pin2
  N2: RESET.pin1, 74ls161-0.pin9, 74ls161-1.pin9, 74ls161-2.pin9, 74ls161-3.pin9, 74ls161-4.pin9
  N3: 74ls161-0.pin1, 74ls161-0.pin3, 74ls161-0.pin7, 74ls161-0.pin10, 74ls161-0.pin16, 74ls161-1.pin1, 74ls161-1.pin16, 74ls161-2.pin1, 74ls161-2.pin16, 74ls161-3.pin1, 74ls161-3.pin16, 74ls161-4.pin1, 74ls161-4.pin16, J6.pin3, J6.pin4
  N4: 74ls161-0.pin4, 74ls161-0.pin5, 74ls161-0.pin6, 74ls161-0.pin8, 74ls161-1.pin3, 74ls161-1.pin4, 74ls161-1.pin5, 74ls161-1.pin6, 74ls161-1.pin8, 74ls161-2.pin3, 74ls161-2.pin4, 74ls161-2.pin5, 74ls161-2.pin6, 74ls161-2.pin8, 74ls161-3.pin3, 74ls161-3.pin4, 74ls161-3.pin5, 74ls161-3.pin6, 74ls161-3.pin8, 74ls161-4.pin3, 74ls161-4.pin4, 74ls161-4.pin5, 74ls161-4.pin6, 74ls161-4.pin8, J6.pin1, J6.pin2
  N5: 74ls161-0.pin11, J5.pin1
  N6: 74ls161-0.pin12, J5.pin2
  N7: 74ls161-0.pin13, J5.pin3
  N8: 74ls161-0.pin14, J5.pin4
  N9: 74ls161-0.pin15, 74ls161-1.pin7, 74ls161-1.pin10
  N10: 74ls161-1.pin11, J4.pin1
  N11: 74ls161-1.pin12, J4.pin2
  N12: 74ls161-1.pin13, J4.pin3
  N13: 74ls161-1.pin14, J4.pin4
  N14: 74ls161-1.pin15, 74ls161-2.pin7, 74ls161-2.pin10
  N15: 74ls161-2.pin11, J3.pin1
  N16: 74ls161-2.pin12, J3.pin2
  N17: 74ls161-2.pin13, J3.pin3
  N18: 74ls161-2.pin14, J3.pin4
  N19: 74ls161-2.pin15, 74ls161-4.pin7, 74ls161-4.pin10
  N20: 74ls161-3.pin7, 74ls161-3.pin10, 74ls161-4.pin15
  N21: 74ls161-3.pin11, J1.pin1
  N22: 74ls161-3.pin12, J1.pin2
  N23: 74ls161-3.pin13, J1.pin3
  N24: 74ls161-3.pin14, J1.pin4
  N25: 74ls161-4.pin11, J2.pin1
  N26: 74ls161-4.pin12, J2.pin2
  N27: 74ls161-4.pin13, J2.pin3
  N28: 74ls161-4.pin14, J2.pin4
