# Fritzing sketch decoder_10x10cm (saved by Fritzing 0.9.1b)
circuit board: 9.95544cm x 7.63772cm
breadboards: 1

parts:
  J5 = female pin header, 4 pins [form="♀ (female)"]
  J6 = female pin header, 4 pins [form="♀ (female)"]
  J7 = female pin header, 4 pins [form="♀ (female)"]
  J8 = female pin header, 4 pins [form="♀ (female)"]
  J9 = female pin header, 11 pins [form="♀ (female)"]
  J11 = female pin header, 11 pins [form="♀ (female)"]
  J14 = female pin header, 12 pins [form="♀ (female)"]
  J15 = female pin header, 12 pins [form="♀ (female)"]
  J16 = female pin header, 12 pins [form="♀ (female)"]
  J17 = female pin header, 12 pins [form="♀ (female)"]
  J18 = female pin header, 2 pins [form="♀ (female)"]  # not connected
  J19 = female pin header, 2 pins [form="♀ (female)"]  # not connected
  J20 = female pin header, 2 pins [form="♀ (female)"]  # not connected
  J21 = female pin header, 2 pins [form="♀ (female)"]  # not connected
  J22 = female pin header, 2 pins [form="♀ (female)"]  # not connected
  J23 = female pin header, 2 pins [form="♀ (female)"]  # not connected
  J24 = female pin header, 4 pins [form="♀ (female)"]
  J25 = female pin header, 4 pins [form="♀ (female)"]
  J26 = female pin header, 4 pins [form="♀ (female)"]
  J27 = female pin header, 4 pins [form="♀ (female)"]
  J28 = female pin header, 2 pins [form="♀ (female)"]  # not connected
  J34 = female pin header, 2 pins [form="♀ (female)"]  # not connected

nets:
  N1: J5.pin1, J16.pin4, J26.pin1
  N2: J5.pin2, J16.pin3, J26.pin2
  N3: J5.pin3, J16.pin2, J26.pin3
  N4: J5.pin4, J17.pin1, J26.pin4
  N5: J6.pin1, J14.pin1, J25.pin1
  N6: J6.pin2, J15.pin2, J25.pin2
  N7: J6.pin3, J15.pin3, J25.pin3
  N8: J6.pin4, J15.pin4, J25.pin4
  N9: J7.pin1, J17.pin2, J24.pin1
  N10: J7.pin2, J17.pin3, J24.pin2
  N11: J7.pin3, J17.pin4, J24.pin3
  N12: J7.pin4, J17.pin5, J24.pin4
  N13: J8.pin1, J14.pin5, J27.pin1
  N14: J8.pin2, J14.pin4, J27.pin2
  N15: J8.pin3, J14.pin3, J27.pin3
  N16: J8.pin4, J14.pin2, J27.pin4
  N17: J9.pin1, J11.pin1, J15.pin5, J16.pin5
  N18: J9.pin2, J11.pin2, J15.pin6, J16.pin6
  N19: J9.pin3, J11.pin3, J15.pin7, J16.pin7
  N20: J9.pin4, J11.pin4, J15.pin8, J16.pin8
  N21: J9.pin5, J11.pin5, J15.pin9, J16.pin9
  N22: J9.pin6, J11.pin6, J15.pin10, J16.pin10
  N23: J9.pin7, J11.pin7, J15.pin11, J16.pin11
  N24: J9.pin8, J11.pin8, J15.pin12, J16.pin12
  N25: J9.pin9, J11.pin9, J14.pin11, J17.pin11
  N26: J9.pin10, J11.pin10, J14.pin10, J17.pin10
  N27: J9.pin11, J11.pin11, J14.pin7, J17.pin7
  N28: J14.pin6, J14.pin8, J15.pin1, J16.pin1, J17.pin6, J17.pin8
  N29: J14.pin9, J14.pin12, J17.pin9, J17.pin12

notes:
  +
  -
  Decoder 2x8bit
  Marius Krabset 2019
  0 1 2 3 4 5 6 7
  input
