# Fritzing sketch outregdisp_v2 (saved by Fritzing 0.9.1b)
circuit board: 9.99cm x 9.99cm
breadboards: 1

parts:
  555 = 555 Timer [package="DIP8 [THT]"]
  74LS163 = IC, DIP package, 16 pins [chip_label=IC]
  C1 = Ceramic Capacitor [capacitance=100nF package="100 mil [THT, multilayer]"]
  74LS139 = IC, DIP package, 16 pins [chip_label=IC]
  C2 = Ceramic Capacitor [capacitance=100nF package="100 mil [THT, multilayer]"]
  display-3 = female pin header, 6 pins [form="♀ (female)"]
  display-4 = female pin header, 6 pins [form="♀ (female)"]
  R2 = Resistor [tolerance=±5% resistance=220 package="1206 [SMD]"]
  R1 = Resistor [tolerance=±5% resistance=220 package="1206 [SMD]"]
  J54 = female pin header, 8 pins [form="♀ (female)"]
  R19 = Resistor [tolerance=±5% resistance=220 package="1206 [SMD]"]
  R20 = Resistor [tolerance=±5% resistance=220 package="1206 [SMD]"]
  R21 = Resistor [tolerance=±5% resistance=220 package="1206 [SMD]"]
  R22 = Resistor [tolerance=±5% resistance=220 package="1206 [SMD]"]
  R23 = Resistor [tolerance=±5% resistance=220 package="1206 [SMD]"]
  R24 = Resistor [tolerance=±5% resistance=220 package="1206 [SMD]"]
  R25 = Resistor [tolerance=±5% resistance=220 package="1206 [SMD]"]
  R26 = Resistor [tolerance=±5% resistance=220 package="1206 [SMD]"]
  IC16 = TSSOP20 [chip_label=IC package=TSSOP]
  J48 = female pin header, 14 pins [form="♀ (female)"]
  J47 = female pin header, 14 pins [form="♀ (female)"]
  R27 = Resistor [tolerance=±5% resistance=220 package="1206 [SMD]"]
  R28 = Resistor [tolerance=±5% resistance=220 package="1206 [SMD]"]
  R29 = Resistor [tolerance=±5% resistance=220 package="1206 [SMD]"]
  R30 = Resistor [tolerance=±5% resistance=220 package="1206 [SMD]"]
  R31 = Resistor [tolerance=±5% resistance=220 package="1206 [SMD]"]
  R32 = Resistor [tolerance=±5% resistance=220 package="1206 [SMD]"]
  R33 = Resistor [tolerance=±5% resistance=220 package="1206 [SMD]"]
  R34 = Resistor [tolerance=±5% resistance=220 package="1206 [SMD]"]
  IC17 = TSSOP20 [chip_label=IC package=TSSOP]
  display-5 = female pin header, 6 pins [form="♀ (female)"]
  display-6 = female pin header, 6 pins [form="♀ (female)"]
  R35 = Resistor [tolerance=±5% resistance=220 package="1206 [SMD]"]
  R36 = Resistor [tolerance=±5% resistance=220 package="1206 [SMD]"]
  R37 = Resistor [tolerance=±5% resistance=220 package="1206 [SMD]"]
  R38 = Resistor [tolerance=±5% resistance=220 package="1206 [SMD]"]
  R39 = Resistor [tolerance=±5% resistance=220 package="1206 [SMD]"]
  R40 = Resistor [tolerance=±5% resistance=220 package="1206 [SMD]"]
  R41 = Resistor [tolerance=±5% resistance=220 package="1206 [SMD]"]
  R42 = Resistor [tolerance=±5% resistance=220 package="1206 [SMD]"]
  IC18 = TSSOP20 [chip_label=IC package=TSSOP]
  display-7 = female pin header, 6 pins [form="♀ (female)"]
  display-8 = female pin header, 6 pins [form="♀ (female)"]
  R43 = Resistor [tolerance=±5% resistance=220 package="1206 [SMD]"]
  R44 = Resistor [tolerance=±5% resistance=220 package="1206 [SMD]"]
  R45 = Resistor [tolerance=±5% resistance=220 package="1206 [SMD]"]
  R46 = Resistor [tolerance=±5% resistance=220 package="1206 [SMD]"]
  R47 = Resistor [tolerance=±5% resistance=220 package="1206 [SMD]"]
  R48 = Resistor [tolerance=±5% resistance=220 package="1206 [SMD]"]
  R49 = Resistor [tolerance=±5% resistance=220 package="1206 [SMD]"]
  R50 = Resistor [tolerance=±5% resistance=220 package="1206 [SMD]"]
  IC19 = TSSOP20 [chip_label=IC package=TSSOP]
  display-9 = female pin header, 6 pins [form="♀ (female)"]
  display-10 = female pin header, 6 pins [form="♀ (female)"]
  R51 = Resistor [tolerance=±5% resistance=220 package="1206 [SMD]"]
  R52 = Resistor [tolerance=±5% resistance=220 package="1206 [SMD]"]
  R53 = Resistor [tolerance=±5% resistance=220 package="1206 [SMD]"]
  R54 = Resistor [tolerance=±5% resistance=220 package="1206 [SMD]"]
  R55 = Resistor [tolerance=±5% resistance=220 package="1206 [SMD]"]
  R56 = Resistor [tolerance=±5% resistance=220 package="1206 [SMD]"]
  R57 = Resistor [tolerance=±5% resistance=220 package="1206 [SMD]"]
  R58 = Resistor [tolerance=±5% resistance=220 package="1206 [SMD]"]
  IC20 = TSSOP20 [chip_label=IC package=TSSOP]
  J56 = female pin header, 8 pins [form="♀ (female)"]
  R59 = Resistor [tolerance=±5% resistance=220 package="1206 [SMD]"]
  R60 = Resistor [tolerance=±5% resistance=220 package="1206 [SMD]"]
  R61 = Resistor [tolerance=±5% resistance=220 package="1206 [SMD]"]
  R62 = Resistor [tolerance=±5% resistance=220 package="1206 [SMD]"]
  R63 = Resistor [tolerance=±5% resistance=220 package="1206 [SMD]"]
  R64 = Resistor [tolerance=±5% resistance=220 package="1206 [SMD]"]
  R65 = Resistor [tolerance=±5% resistance=220 package="1206 [SMD]"]
  R66 = Resistor [tolerance=±5% resistance=220 package="1206 [SMD]"]
  IC21 = TSSOP20 [chip_label=IC package=TSSOP]
  J57 = female pin header, 8 pins [form="♀ (female)"]
  J58 = female pin header, 8 pins [form="♀ (female)"]
  R67 = Resistor [tolerance=±5% resistance=220 package="1206 [SMD]"]
  R68 = Resistor [tolerance=±5% resistance=220 package="1206 [SMD]"]
  R69 = Resistor [tolerance=±5% resistance=220 package="1206 [SMD]"]
  R70 = Resistor [tolerance=±5% resistance=220 package="1206 [SMD]"]
  R71 = Resistor [tolerance=±5% resistance=220 package="1206 [SMD]"]
  R72 = Resistor [tolerance=±5% resistance=220 package="1206 [SMD]"]
  R73 = Resistor [tolerance=±5% resistance=220 package="1206 [SMD]"]
  R74 = Resistor [tolerance=±5% resistance=220 package="1206 [SMD]"]
  R75 = Resistor [tolerance=±5% resistance=220 package="1206 [SMD]"]
  R76 = Resistor [tolerance=±5% resistance=220 package="1206 [SMD]"]
  R77 = Resistor [tolerance=±5% resistance=220 package="1206 [SMD]"]
  R78 = Resistor [tolerance=±5% resistance=220 package="1206 [SMD]"]
  R79 = Resistor [tolerance=±5% resistance=220 package="1206 [SMD]"]
  R80 = Resistor [tolerance=±5% resistance=220 package="1206 [SMD]"]
  R81 = Resistor [tolerance=±5% resistance=220 package="1206 [SMD]"]
  R82 = Resistor [tolerance=±5% resistance=220 package="1206 [SMD]"]
  IC22 = TSSOP20 [chip_label=IC package=TSSOP]
  IC23 = TSSOP20 [chip_label=IC package=TSSOP]

nets:
  N1: 555.Ground, 74LS163.pin8, C1.1, 74LS139.pin1, 74LS139.pin8, 74LS139.pin15, C2.0
  N2: 555.Trigger, 555.Threshold, C1.0, R2.Pin_0
  N3: 555.Output, 74LS163.pin2
  N4: 555.Discharge, R2.Pin_1, R1.Pin_0
  N5: 555.Vcc_Supply_Voltage, 74LS163.pin1, 74LS163.pin7, 74LS163.pin9, 74LS163.pin10, 74LS163.pin16, 74LS139.pin16, C2.1, R1.Pin_1
  N6: 74LS163.pin11, 74LS139.pin13
  N7: 74LS163.pin12, 74LS139.pin14
  N8: 74LS163.pin13, 74LS139.pin3
  N9: 74LS163.pin14, 74LS139.pin2
  N10: 74LS139.pin4, display-4.pin1, display-6.pin1, display-8.pin1, display-10.pin1
  N11: 74LS139.pin5, display-4.pin4, display-6.pin4, display-8.pin4, display-10.pin4
  N12: 74LS139.pin6, display-4.pin5, display-6.pin5, display-8.pin5, display-10.pin5
  N13: 74LS139.pin7, display-3.pin6, display-5.pin6, display-7.pin6, display-9.pin6
  N14: 74LS139.pin9, IC20.19, IC23.19
  N15: 74LS139.pin10, IC19.19, IC22.19
  N16: 74LS139.pin11, IC18.19, IC21.19
  N17: 74LS139.pin12, IC16.19, IC17.19
  N18: display-3.pin1, R30.Pin_1
  N19: display-3.pin2, R31.Pin_1
  N20: display-3.pin3, R29.Pin_1
  N21: display-3.pin4, R32.Pin_1
  N22: display-3.pin5, R27.Pin_1
  N23: display-4.pin2, R34.Pin_1
  N24: display-4.pin3, R28.Pin_1
  N25: display-4.pin6, R33.Pin_1
  N26: J54.pin1, IC16.2
  N27: J54.pin2, IC16.3
  N28: J54.pin3, IC16.4
  N29: J54.pin4, IC16.5
  N30: J54.pin5, IC16.6
  N31: J54.pin6, IC16.7
  N32: J54.pin7, IC16.8
  N33: J54.pin8, IC16.9
  N34: R19.Pin_0, IC16.12
  N35: R19.Pin_1, J48.pin9, R59.Pin_1, R67.Pin_1, R68.Pin_1
  N36: R20.Pin_0, IC16.13
  N37: R20.Pin_1, J48.pin8, R60.Pin_1, R69.Pin_1, R70.Pin_1
  N38: R21.Pin_0, IC16.11
  N39: R21.Pin_1, J48.pin10, R61.Pin_1, R71.Pin_1, R72.Pin_1
  N40: R22.Pin_0, IC16.14
  N41: R22.Pin_1, J48.pin7, R62.Pin_1, R73.Pin_1, R74.Pin_1
  N42: R23.Pin_0, IC16.15
  N43: R23.Pin_1, J48.pin6, R63.Pin_1, R75.Pin_1, R76.Pin_1
  N44: R24.Pin_0, IC16.16
  N45: R24.Pin_1, J48.pin5, R64.Pin_1, R77.Pin_1, R78.Pin_1
  N46: R25.Pin_0, IC16.17
  N47: R25.Pin_1, J48.pin4, R65.Pin_1, R79.Pin_1, R80.Pin_1
  N48: R26.Pin_0, IC16.18
  N49: R26.Pin_1, J48.pin3, R66.Pin_1, R81.Pin_1, R82.Pin_1
  N50: IC16.1, IC16.20, IC21.1, IC21.20, IC22.1, IC22.20, IC23.1, IC23.20
  N51: IC16.10, IC21.10, IC22.10, IC23.10
  N52: J47.pin1, J47.pin2
  N53: R27.Pin_0, IC17.12
  N54: R28.Pin_0, IC17.13
  N55: R29.Pin_0, IC17.11
  N56: R30.Pin_0, IC17.14
  N57: R31.Pin_0, IC17.15
  N58: R32.Pin_0, IC17.16
  N59: R33.Pin_0, IC17.17
  N60: R34.Pin_0, IC17.18
  N61: IC17.1, IC17.20, IC18.1, IC18.20, IC19.1, IC19.20, IC20.1, IC20.20
  N62: IC17.2, IC18.2, IC19.2, IC20.2
  N63: IC17.3, IC18.3, IC19.3, IC20.3
  N64: IC17.4, IC18.4, IC19.4, IC20.4
  N65: IC17.5, IC18.5, IC19.5, IC20.5
  N66: IC17.6, IC18.6, IC19.6, IC20.6
  N67: IC17.7, IC18.7, IC19.7, IC20.7
  N68: IC17.8, IC18.8, IC19.8, IC20.8
  N69: IC17.9, IC18.9, IC19.9, IC20.9
  N70: IC17.10, IC18.10, IC19.10, IC20.10
  N71: display-5.pin1, R38.Pin_1
  N72: display-5.pin2, R39.Pin_1
  N73: display-5.pin3, R37.Pin_1
  N74: display-5.pin4, R40.Pin_1
  N75: display-5.pin5, R35.Pin_1
  N76: display-6.pin2, R42.Pin_1
  N77: display-6.pin3, R36.Pin_1
  N78: display-6.pin6, R41.Pin_1
  N79: R35.Pin_0, IC18.12
  N80: R36.Pin_0, IC18.13
  N81: R37.Pin_0, IC18.11
  N82: R38.Pin_0, IC18.14
  N83: R39.Pin_0, IC18.15
  N84: R40.Pin_0, IC18.16
  N85: R41.Pin_0, IC18.17
  N86: R42.Pin_0, IC18.18
  N87: display-7.pin1, R46.Pin_1
  N88: display-7.pin2, R47.Pin_1
  N89: display-7.pin3, R45.Pin_1
  N90: display-7.pin4, R48.Pin_1
  N91: display-7.pin5, R43.Pin_1
  N92: display-8.pin2, R50.Pin_1
  N93: display-8.pin3, R44.Pin_1
  N94: display-8.pin6, R49.Pin_1
  N95: R43.Pin_0, IC19.12
  N96: R44.Pin_0, IC19.13
  N97: R45.Pin_0, IC19.11
  N98: R46.Pin_0, IC19.14
  N99: R47.Pin_0, IC19.15
  N100: R48.Pin_0, IC19.16
  N101: R49.Pin_0, IC19.17
  N102: R50.Pin_0, IC19.18
  N103: display-9.pin1, R54.Pin_1
  N104: display-9.pin2, R55.Pin_1
  N105: display-9.pin3, R53.Pin_1
  N106: display-9.pin4, R56.Pin_1
  N107: display-9.pin5, R51.Pin_1
  N108: display-10.pin2, R58.Pin_1
  N109: display-10.pin3, R52.Pin_1
  N110: display-10.pin6, R57.Pin_1
  N111: R51.Pin_0, IC20.12
  N112: R52.Pin_0, IC20.13
  N113: R53.Pin_0, IC20.11
  N114: R54.Pin_0, IC20.14
  N115: R55.Pin_0, IC20.15
  N116: R56.Pin_0, IC20.16
  N117: R57.Pin_0, IC20.17
  N118: R58.Pin_0, IC20.18
  N119: J56.pin1, IC21.2
  N120: J56.pin2, IC21.3
  N121: J56.pin3, IC21.4
  N122: J56.pin4, IC21.5
  N123: J56.pin5, IC21.6
  N124: J56.pin6, IC21.7
  N125: J56.pin7, IC21.8
  N126: J56.pin8, IC21.9
  N127: R59.Pin_0, IC21.12
  N128: R60.Pin_0, IC21.13
  N129: R61.Pin_0, IC21.11
  N130: R62.Pin_0, IC21.14
  N131: R63.Pin_0, IC21.15
  N132: R64.Pin_0, IC21.16
  N133: R65.Pin_0, IC21.17
  N134: R66.Pin_0, IC21.18
  N135: J57.pin1, IC22.2
  N136: J57.pin2, IC22.3
  N137: J57.pin3, IC22.4
  N138: J57.pin4, IC22.5
  N139: J57.pin5, IC22.6
  N140: J57.pin6, IC22.7
  N141: J57.pin7, IC22.8
  N142: J57.pin8, IC22.9
  N143: J58.pin1, IC23.2
  N144: J58.pin2, IC23.3
  N145: J58.pin3, IC23.4
  N146: J58.pin4, IC23.5
  N147: J58.pin5, IC23.6
  N148: J58.pin6, IC23.7
  N149: J58.pin7, IC23.8
  N150: J58.pin8, IC23.9
  N151: R67.Pin_0, IC22.12
  N152: R68.Pin_0, IC23.12
  N153: R69.Pin_0, IC22.13
  N154: R70.Pin_0, IC23.13
  N155: R71.Pin_0, IC22.11
  N156: R72.Pin_0, IC23.11
  N157: R73.Pin_0, IC22.14
  N158: R74.Pin_0, IC23.14
  N159: R75.Pin_0, IC22.15
  N160: R76.Pin_0, IC23.15
  N161: R77.Pin_0, IC22.16
  N162: R78.Pin_0, IC23.16
  N163: R79.Pin_0, IC22.17
  N164: R80.Pin_0, IC23.17
  N165: R81.Pin_0, IC22.18
  N166: R82.Pin_0, IC23.18
