# Fritzing sketch outregdisp_v2_wsop20 (saved by Fritzing 0.9.1b)
circuit board: 9.99cm x 9.99cm
breadboards: 1

parts:
  555 = 555 Timer [package="DIP8 [THT]"]
  74LS163 = IC, DIP package, 16 pins [chip_label=IC]
  C1 = Ceramic Capacitor [capacitance=100nF package="100 mil [THT, multilayer]"]
  74LS139 = IC, DIP package, 16 pins [chip_label=IC]
  C2 = Ceramic Capacitor [capacitance=100nF package="100 mil [THT, multilayer]"]
  R2 = Resistor [tolerance=±5% resistance=220 package="1206 [SMD]"]
  R1 = Resistor [tolerance=±5% resistance=220 package="1206 [SMD]"]
  C3 = Electrolytic Capacitor [capacitance=1µF package="100 mil [THT, electrolytic]"]
  J62 = female pin header, 2 pins [form="♀ (female)"]
  J63 = female pin header, 2 pins [form="♀ (female)"]
  J64 = female pin header, 8 pins [form="♀ (female)"]
  R83 = Resistor [tolerance=±5% resistance=220 package="1206 [SMD]"]
  R84 = Resistor [tolerance=±5% resistance=220 package="1206 [SMD]"]
  R85 = Resistor [tolerance=±5% resistance=220 package="1206 [SMD]"]
  R86 = Resistor [tolerance=±5% resistance=220 package="1206 [SMD]"]
  R87 = Resistor [tolerance=±5% resistance=220 package="1206 [SMD]"]
  R88 = Resistor [tolerance=±5% resistance=220 package="1206 [SMD]"]
  R89 = Resistor [tolerance=±5% resistance=220 package="1206 [SMD]"]
  R90 = Resistor [tolerance=±5% resistance=220 package="1206 [SMD]"]
  IC26 = SO20W [chip_label=IC package=SO(w)]
  J65 = female pin header, 14 pins [form="♀ (female)"]  # not connected
  J66 = female pin header, 14 pins [form="♀ (female)"]  # not connected
  J67 = female pin header, 5 pins [form="♀ (female)"]  # not connected
  display-13 = female pin header, 6 pins [form="♀ (female)"]
  display-14 = female pin header, 6 pins [form="♀ (female)"]
  IC28 = SO20W [chip_label=IC package=SO(w)]
  R103 = Resistor [tolerance=±5% resistance=220 package="1206 [SMD]"]
  R99 = Resistor [tolerance=±5% resistance=220 package="1206 [SMD]"]
  R104 = Resistor [tolerance=±5% resistance=220 package="1206 [SMD]"]
  R105 = Resistor [tolerance=±5% resistance=220 package="1206 [SMD]"]
  R100 = Resistor [tolerance=±5% resistance=220 package="1206 [SMD]"]
  R102 = Resistor [tolerance=±5% resistance=220 package="1206 [SMD]"]
  R101 = Resistor [tolerance=±5% resistance=220 package="1206 [SMD]"]
  R106 = Resistor [tolerance=±5% resistance=220 package="1206 [SMD]"]
  J68 = female pin header, 8 pins [form="♀ (female)"]
  R107 = Resistor [tolerance=±5% resistance=220 package="1206 [SMD]"]
  R108 = Resistor [tolerance=±5% resistance=220 package="1206 [SMD]"]
  R109 = Resistor [tolerance=±5% resistance=220 package="1206 [SMD]"]
  R110 = Resistor [tolerance=±5% resistance=220 package="1206 [SMD]"]
  R111 = Resistor [tolerance=±5% resistance=220 package="1206 [SMD]"]
  R112 = Resistor [tolerance=±5% resistance=220 package="1206 [SMD]"]
  R113 = Resistor [tolerance=±5% resistance=220 package="1206 [SMD]"]
  R114 = Resistor [tolerance=±5% resistance=220 package="1206 [SMD]"]
  IC29 = SO20W [chip_label=IC package=SO(w)]
  J69 = female pin header, 8 pins [form="♀ (female)"]
  R115 = Resistor [tolerance=±5% resistance=220 package="1206 [SMD]"]
  R116 = Resistor [tolerance=±5% resistance=220 package="1206 [SMD]"]
  R117 = Resistor [tolerance=±5% resistance=220 package="1206 [SMD]"]
  R118 = Resistor [tolerance=±5% resistance=220 package="1206 [SMD]"]
  R119 = Resistor [tolerance=±5% resistance=220 package="1206 [SMD]"]
  R120 = Resistor [tolerance=±5% resistance=220 package="1206 [SMD]"]
  R121 = Resistor [tolerance=±5% resistance=220 package="1206 [SMD]"]
  R122 = Resistor [tolerance=±5% resistance=220 package="1206 [SMD]"]
  IC30 = SO20W [chip_label=IC package=SO(w)]
  J77 = female pin header, 8 pins [form="♀ (female)"]  # not connected
  J78 = female pin header, 8 pins [form="♀ (female)"]  # not connected
  J79 = female pin header, 8 pins [form="♀ (female)"]  # not connected
  J80 = female pin header, 8 pins [form="♀ (female)"]
  J81 = female pin header, 8 pins [form="♀ (female)"]  # not connected
  R123 = Resistor [tolerance=±5% resistance=220 package="1206 [SMD]"]
  R124 = Resistor [tolerance=±5% resistance=220 package="1206 [SMD]"]
  R125 = Resistor [tolerance=±5% resistance=220 package="1206 [SMD]"]
  R126 = Resistor [tolerance=±5% resistance=220 package="1206 [SMD]"]
  R127 = Resistor [tolerance=±5% resistance=220 package="1206 [SMD]"]
  R128 = Resistor [tolerance=±5% resistance=220 package="1206 [SMD]"]
  R129 = Resistor [tolerance=±5% resistance=220 package="1206 [SMD]"]
  R130 = Resistor [tolerance=±5% resistance=220 package="1206 [SMD]"]
  IC31 = SO20W [chip_label=IC package=SO(w)]
  J82 = female pin header, 8 pins [form="♀ (female)"]
  R131 = Resistor [tolerance=±5% resistance=220 package="1206 [SMD]"]
  R132 = Resistor [tolerance=±5% resistance=220 package="1206 [SMD]"]
  R133 = Resistor [tolerance=±5% resistance=220 package="1206 [SMD]"]
  R134 = Resistor [tolerance=±5% resistance=220 package="1206 [SMD]"]
  R135 = Resistor [tolerance=±5% resistance=220 package="1206 [SMD]"]
  R136 = Resistor [tolerance=±5% resistance=220 package="1206 [SMD]"]
  R137 = Resistor [tolerance=±5% resistance=220 package="1206 [SMD]"]
  R138 = Resistor [tolerance=±5% resistance=220 package="1206 [SMD]"]
  IC32 = SO20W [chip_label=IC package=SO(w)]
  J83 = female pin header, 14 pins [form="♀ (female)"]  # not connected
  J84 = female pin header, 14 pins [form="♀ (female)"]
  J85 = female pin header, 5 pins [form="♀ (female)"]  # not connected
  IC33 = SO20W [chip_label=IC package=SO(w)]
  R139 = Resistor [tolerance=±5% resistance=220 package="1206 [SMD]"]
  R140 = Resistor [tolerance=±5% resistance=220 package="1206 [SMD]"]
  R141 = Resistor [tolerance=±5% resistance=220 package="1206 [SMD]"]
  R142 = Resistor [tolerance=±5% resistance=220 package="1206 [SMD]"]
  R143 = Resistor [tolerance=±5% resistance=220 package="1206 [SMD]"]
  R144 = Resistor [tolerance=±5% resistance=220 package="1206 [SMD]"]
  R145 = Resistor [tolerance=±5% resistance=220 package="1206 [SMD]"]
  R146 = Resistor [tolerance=±5% resistance=220 package="1206 [SMD]"]
  display-15 = female pin header, 6 pins [form="♀ (female)"]
  display-16 = female pin header, 6 pins [form="♀ (female)"]
  IC34 = SO20W [chip_label=IC package=SO(w)]
  R147 = Resistor [tolerance=±5% resistance=220 package="1206 [SMD]"]
  R148 = Resistor [tolerance=±5% resistance=220 package="1206 [SMD]"]
  R149 = Resistor [tolerance=±5% resistance=220 package="1206 [SMD]"]
  R150 = Resistor [tolerance=±5% resistance=220 package="1206 [SMD]"]
  R151 = Resistor [tolerance=±5% resistance=220 package="1206 [SMD]"]
  R152 = Resistor [tolerance=±5% resistance=220 package="1206 [SMD]"]
  R153 = Resistor [tolerance=±5% resistance=220 package="1206 [SMD]"]
  R154 = Resistor [tolerance=±5% resistance=220 package="1206 [SMD]"]
  display-17 = female pin header, 6 pins [form="♀ (female)"]
  display-18 = female pin header, 6 pins [form="♀ (female)"]
  IC35 = SO20W [chip_label=IC package=SO(w)]
  IC36 = SO20W [chip_label=IC package=SO(w)]
  R155 = Resistor [tolerance=±5% resistance=220 package="1206 [SMD]"]
  R156 = Resistor [tolerance=±5% resistance=220 package="1206 [SMD]"]
  R157 = Resistor [tolerance=±5% resistance=220 package="1206 [SMD]"]
  R158 = Resistor [tolerance=±5% resistance=220 package="1206 [SMD]"]
  R159 = Resistor [tolerance=±5% resistance=220 package="1206 [SMD]"]
  R160 = Resistor [tolerance=±5% resistance=220 package="1206 [SMD]"]
  R161 = Resistor [tolerance=±5% resistance=220 package="1206 [SMD]"]
  R162 = Resistor [tolerance=±5% resistance=220 package="1206 [SMD]"]
  R163 = Resistor [tolerance=±5% resistance=220 package="1206 [SMD]"]
  R164 = Resistor [tolerance=±5% resistance=220 package="1206 [SMD]"]
  R165 = Resistor [tolerance=±5% resistance=220 package="1206 [SMD]"]
  R166 = Resistor [tolerance=±5% resistance=220 package="1206 [SMD]"]
  R167 = Resistor [tolerance=±5% resistance=220 package="1206 [SMD]"]
  R168 = Resistor [tolerance=±5% resistance=220 package="1206 [SMD]"]
  R169 = Resistor [tolerance=±5% resistance=220 package="1206 [SMD]"]
  R170 = Resistor [tolerance=±5% resistance=220 package="1206 [SMD]"]
  display-19 = female pin header, 6 pins [form="♀ (female)"]
  display-20 = female pin header, 6 pins [form="♀ (female)"]
  display-21 = female pin header, 6 pins [form="♀ (female)"]
  display-22 = female pin header, 6 pins [form="♀ (female)"]

nets:
  N1: 555.Ground, 74LS163.pin8, C1.1, 74LS139.pin1, 74LS139.pin8, 74LS139.pin15, C2.0
  N2: 555.Trigger, 555.Threshold, C1.0, R2.Pin_0
  N3: 555.Output, 74LS163.pin2
  N4: 555.Discharge, R2.Pin_1, R1.Pin_0
  N5: 555.Vcc_Supply_Voltage, 74LS163.pin1, 74LS163.pin7, 74LS163.pin9, 74LS163.pin10, 74LS163.pin16, 74LS139.pin16, C2.1, R1.Pin_1
  N6: 74LS163.pin11, 74LS139.pin13
  N7: 74LS163.pin12, 74LS139.pin14
  N8: 74LS163.pin13, 74LS139.pin3
  N9: 74LS163.pin14, 74LS139.pin2
  N10: C3.-, J62.pin1, J63.pin1, IC29.10, IC30.10, IC31.10, IC32.10, J84.pin14
  N11: C3.+, J62.pin2, J63.pin2, IC29.1, IC29.20, IC30.1, IC30.20, IC31.1, IC31.20, IC32.1, IC32.20
  N12: J64.pin1, IC26.2
  N13: J64.pin2, IC26.3
  N14: J64.pin3, IC26.4
  N15: J64.pin4, IC26.5
  N16: J64.pin5, IC26.6
  N17: J64.pin6, IC26.7
  N18: J64.pin7, IC26.8
  N19: J64.pin8, IC26.9
  N20: R83.Pin_0, IC26.12
  N21: R84.Pin_0, IC26.13
  N22: R85.Pin_0, IC26.11
  N23: R86.Pin_0, IC26.14
  N24: R87.Pin_0, IC26.15
  N25: R88.Pin_0, IC26.16
  N26: R89.Pin_0, IC26.17
  N27: R90.Pin_0, IC26.18
  N28: IC26.1, IC26.20
  N29: display-13.pin1, R106.Pin_0
  N30: display-13.pin2, R105.Pin_0
  N31: display-13.pin3, R101.Pin_0
  N32: display-13.pin4, R100.Pin_1
  N33: display-13.pin5, R102.Pin_0
  N34: display-14.pin2, R103.Pin_0
  N35: display-14.pin3, R104.Pin_0
  N36: display-14.pin6, R99.Pin_0
  N37: IC28.1, IC28.10
  N38: IC28.2, R103.Pin_1
  N39: IC28.3, R99.Pin_1
  N40: IC28.4, R100.Pin_0
  N41: IC28.5, R105.Pin_1
  N42: IC28.6, R106.Pin_1
  N43: IC28.7, R104.Pin_1
  N44: IC28.8, R102.Pin_1
  N45: IC28.9, R101.Pin_1
  N46: J68.pin1, IC29.2
  N47: J68.pin2, IC29.3
  N48: J68.pin3, IC29.4
  N49: J68.pin4, IC29.5
  N50: J68.pin5, IC29.6
  N51: J68.pin6, IC29.7
  N52: J68.pin7, IC29.8
  N53: J68.pin8, IC29.9
  N54: R107.Pin_0, IC29.12
  N55: R107.Pin_1, R115.Pin_1, R123.Pin_1, R131.Pin_1, J84.pin9
  N56: R108.Pin_0, IC29.13
  N57: R108.Pin_1, R116.Pin_1, R124.Pin_1, R132.Pin_1, J84.pin8
  N58: R109.Pin_0, IC29.11
  N59: R109.Pin_1, R117.Pin_1, R125.Pin_1, R133.Pin_1, J84.pin10
  N60: R110.Pin_0, IC29.14
  N61: R110.Pin_1, R118.Pin_1, R126.Pin_1, R134.Pin_1, J84.pin7
  N62: R111.Pin_0, IC29.15
  N63: R111.Pin_1, R119.Pin_1, R127.Pin_1, R135.Pin_1, J84.pin6
  N64: R112.Pin_0, IC29.16
  N65: R112.Pin_1, R120.Pin_1, R128.Pin_1, R136.Pin_1, J84.pin5
  N66: R113.Pin_0, IC29.17
  N67: R113.Pin_1, R121.Pin_1, R129.Pin_1, R137.Pin_1, J84.pin4
  N68: R114.Pin_0, IC29.18
  N69: R114.Pin_1, R122.Pin_1, R130.Pin_1, R138.Pin_1, J84.pin3
  N70: J69.pin1, IC30.2
  N71: J69.pin2, IC30.3
  N72: J69.pin3, IC30.4
  N73: J69.pin4, IC30.5
  N74: J69.pin5, IC30.6
  N75: J69.pin6, IC30.7
  N76: J69.pin7, IC30.8
  N77: J69.pin8, IC30.9
  N78: R115.Pin_0, IC30.12
  N79: R116.Pin_0, IC30.13
  N80: R117.Pin_0, IC30.11
  N81: R118.Pin_0, IC30.14
  N82: R119.Pin_0, IC30.15
  N83: R120.Pin_0, IC30.16
  N84: R121.Pin_0, IC30.17
  N85: R122.Pin_0, IC30.18
  N86: J80.pin1, IC31.2
  N87: J80.pin2, IC31.3
  N88: J80.pin3, IC31.4
  N89: J80.pin4, IC31.5
  N90: J80.pin5, IC31.6
  N91: J80.pin6, IC31.7
  N92: J80.pin7, IC31.8
  N93: J80.pin8, IC31.9
  N94: R123.Pin_0, IC31.12
  N95: R124.Pin_0, IC31.13
  N96: R125.Pin_0, IC31.11
  N97: R126.Pin_0, IC31.14
  N98: R127.Pin_0, IC31.15
  N99: R128.Pin_0, IC31.16
  N100: R129.Pin_0, IC31.17
  N101: R130.Pin_0, IC31.18
  N102: J82.pin2, IC32.3
  N103: J82.pin3, IC32.4
  N104: J82.pin4, IC32.5
  N105: J82.pin5, IC32.6
  N106: J82.pin6, IC32.7
  N107: J82.pin7, IC32.8
  N108: J82.pin8, IC32.9
  N109: R131.Pin_0, IC32.12
  N110: R132.Pin_0, IC32.13
  N111: R133.Pin_0, IC32.11
  N112: R134.Pin_0, IC32.14
  N113: R135.Pin_0, IC32.15
  N114: R136.Pin_0, IC32.16
  N115: R137.Pin_0, IC32.17
  N116: R138.Pin_0, IC32.18
  N117: IC33.1, IC33.10, IC34.1, IC34.10, IC35.1, IC35.10, IC36.1, IC36.10
  N118: IC33.2, R139.Pin_1
  N119: IC33.3, R140.Pin_1
  N120: IC33.4, R143.Pin_0
  N121: IC33.5, R142.Pin_1
  N122: IC33.6, R146.Pin_1
  N123: IC33.7, R141.Pin_1
  N124: IC33.8, R144.Pin_1
  N125: IC33.9, R145.Pin_1
  N126: IC33.20, IC34.20, IC35.20, IC36.20
  N127: R139.Pin_0, display-16.pin2
  N128: R140.Pin_0, display-16.pin6
  N129: R141.Pin_0, display-16.pin3
  N130: R142.Pin_0, display-15.pin2
  N131: R143.Pin_1, display-15.pin4
  N132: R144.Pin_0, display-15.pin5
  N133: R145.Pin_0, display-15.pin3
  N134: R146.Pin_0, display-15.pin1
  N135: display-15.pin6, display-17.pin6, display-19.pin6, display-20.pin6
  N136: display-16.pin1, display-18.pin1, display-21.pin1, display-22.pin1
  N137: display-16.pin4, display-18.pin4, display-21.pin4, display-22.pin4
  N138: display-16.pin5, display-18.pin5, display-21.pin5, display-22.pin5
  N139: IC34.2, R147.Pin_1
  N140: IC34.3, R148.Pin_1
  N141: IC34.4, R151.Pin_0
  N142: IC34.5, R150.Pin_1
  N143: IC34.6, R154.Pin_1
  N144: IC34.7, R149.Pin_1
  N145: IC34.8, R152.Pin_1
  N146: IC34.9, R153.Pin_1
  N147: R147.Pin_0, display-18.pin2
  N148: R148.Pin_0, display-18.pin6
  N149: R149.Pin_0, display-18.pin3
  N150: R150.Pin_0, display-17.pin2
  N151: R151.Pin_1, display-17.pin4
  N152: R152.Pin_0, display-17.pin5
  N153: R153.Pin_0, display-17.pin3
  N154: R154.Pin_0, display-17.pin1
  N155: IC35.2, R156.Pin_1
  N156: IC35.3, R158.Pin_1
  N157: IC35.4, R163.Pin_0
  N158: IC35.5, R162.Pin_1
  N159: IC35.6, R170.Pin_1
  N160: IC35.7, R160.Pin_1
  N161: IC35.8, R165.Pin_1
  N162: IC35.9, R168.Pin_1
  N163: IC36.2, R155.Pin_1
  N164: IC36.3, R157.Pin_1
  N165: IC36.4, R164.Pin_0
  N166: IC36.5, R161.Pin_1
  N167: IC36.6, R169.Pin_1
  N168: IC36.7, R159.Pin_1
  N169: IC36.8, R166.Pin_1
  N170: IC36.9, R167.Pin_1
  N171: R155.Pin_0, display-21.pin2
  N172: R156.Pin_0, display-22.pin2
  N173: R157.Pin_0, display-21.pin6
  N174: R158.Pin_0, display-22.pin6
  N175: R159.Pin_0, display-21.pin3
  N176: R160.Pin_0, display-22.pin3
  N177: R161.Pin_0, display-19.pin2
  N178: R162.Pin_0, display-20.pin2
  N179: R163.Pin_1, display-20.pin4
  N180: R164.Pin_1, display-19.pin4
  N181: R165.Pin_0, display-20.pin5
  N182: R166.Pin_0, display-19.pin5
  N183: R167.Pin_0, display-19.pin3
  N184: R168.Pin_0, display-20.pin3
  N185: R169.Pin_0, display-19.pin1
  N186: R170.Pin_0, display-20.pin1

notes:
  OUTPUT REGISTERS
  Marius Krabset 2019
  -
  +
