# Fritzing sketch sigdisplay (saved by Fritzing 0.9.1b)
circuit board: 9.95544cm x 7.63772cm
breadboards: 1

parts:
  IC1 = IC, DIP package, 20 pins [chip_label=IC]
  IC2 = IC, DIP package, 20 pins [chip_label=IC]
  IC3 = IC, DIP package, 20 pins [chip_label=IC]
  IC4 = IC, DIP package, 20 pins [chip_label=IC]
  J1 = female pin header, 8 pins [form="♀ (female)"]
  J2 = female pin header, 8 pins [form="♀ (female)"]
  J3 = female pin header, 8 pins [form="♀ (female)"]
  J4 = female pin header, 8 pins [form="♀ (female)"]
  LEDS = IC, DIP package, 16 pins [chip_label=IC]
  R1 = Resistor [tolerance=±5% resistance=220 package="1206 [SMD]"]
  R2 = Resistor [tolerance=±5% resistance=220 package="1206 [SMD]"]
  R3 = Resistor [tolerance=±5% resistance=220 package="1206 [SMD]"]
  R4 = Resistor [tolerance=±5% resistance=220 package="1206 [SMD]"]
  R5 = Resistor [tolerance=±5% resistance=220 package="1206 [SMD]"]
  R6 = Resistor [tolerance=±5% resistance=220 package="1206 [SMD]"]
  R7 = Resistor [tolerance=±5% resistance=220 package="1206 [SMD]"]
  R8 = Resistor [tolerance=±5% resistance=220 package="1206 [SMD]"]
  LEDS1 = IC, DIP package, 16 pins [chip_label=IC]
  R9 = Resistor [tolerance=±5% resistance=220 package="1206 [SMD]"]
  R10 = Resistor [tolerance=±5% resistance=220 package="1206 [SMD]"]
  R11 = Resistor [tolerance=±5% resistance=220 package="1206 [SMD]"]
  R12 = Resistor [tolerance=±5% resistance=220 package="1206 [SMD]"]
  R13 = Resistor [tolerance=±5% resistance=220 package="1206 [SMD]"]
  R14 = Resistor [tolerance=±5% resistance=220 package="1206 [SMD]"]
  R15 = Resistor [tolerance=±5% resistance=220 package="1206 [SMD]"]
  R16 = Resistor [tolerance=±5% resistance=220 package="1206 [SMD]"]
  LEDS2 = IC, DIP package, 16 pins [chip_label=IC]
  R17 = Resistor [tolerance=±5% resistance=220 package="1206 [SMD]"]
  R18 = Resistor [tolerance=±5% resistance=220 package="1206 [SMD]"]
  R19 = Resistor [tolerance=±5% resistance=220 package="1206 [SMD]"]
  R20 = Resistor [tolerance=±5% resistance=220 package="1206 [SMD]"]
  R21 = Resistor [tolerance=±5% resistance=220 package="1206 [SMD]"]
  R22 = Resistor [tolerance=±5% resistance=220 package="1206 [SMD]"]
  R23 = Resistor [tolerance=±5% resistance=220 package="1206 [SMD]"]
  R24 = Resistor [tolerance=±5% resistance=220 package="1206 [SMD]"]
  LEDS3 = IC, DIP package, 16 pins [chip_label=IC]
  R25 = Resistor [tolerance=±5% resistance=220 package="1206 [SMD]"]
  R26 = Resistor [tolerance=±5% resistance=220 package="1206 [SMD]"]
  R27 = Resistor [tolerance=±5% resistance=220 package="1206 [SMD]"]
  R28 = Resistor [tolerance=±5% resistance=220 package="1206 [SMD]"]
  R29 = Resistor [tolerance=±5% resistance=220 package="1206 [SMD]"]
  R30 = Resistor [tolerance=±5% resistance=220 package="1206 [SMD]"]
  R31 = Resistor [tolerance=±5% resistance=220 package="1206 [SMD]"]
  R32 = Resistor [tolerance=±5% resistance=220 package="1206 [SMD]"]

nets:
  N1: IC1.pin2, LEDS.pin16
  N2: IC1.pin3, LEDS.pin15
  N3: IC1.pin4, LEDS.pin14
  N4: IC1.pin5, LEDS.pin13
  N5: IC1.pin6, LEDS.pin12
  N6: IC1.pin7, LEDS.pin11
  N7: IC1.pin8, LEDS.pin10
  N8: IC1.pin9, LEDS.pin9
  N9: IC1.pin11, J1.pin8
  N10: IC1.pin12, J1.pin7
  N11: IC1.pin13, J1.pin6
  N12: IC1.pin14, J1.pin5
  N13: IC1.pin15, J1.pin4
  N14: IC1.pin16, J1.pin3
  N15: IC1.pin17, J1.pin2
  N16: IC1.pin18, J1.pin1
  N17: IC2.pin2, LEDS1.pin16
  N18: IC2.pin3, LEDS1.pin15
  N19: IC2.pin4, LEDS1.pin14
  N20: IC2.pin5, LEDS1.pin13
  N21: IC2.pin6, LEDS1.pin12
  N22: IC2.pin7, LEDS1.pin11
  N23: IC2.pin8, LEDS1.pin10
  N24: IC2.pin9, LEDS1.pin9
  N25: IC2.pin11, J2.pin8
  N26: IC2.pin12, J2.pin7
  N27: IC2.pin13, J2.pin6
  N28: IC2.pin14, J2.pin5
  N29: IC2.pin15, J2.pin4
  N30: IC2.pin16, J2.pin3
  N31: IC2.pin17, J2.pin2
  N32: IC2.pin18, J2.pin1
  N33: IC3.pin2, LEDS2.pin16
  N34: IC3.pin3, LEDS2.pin15
  N35: IC3.pin4, LEDS2.pin14
  N36: IC3.pin5, LEDS2.pin13
  N37: IC3.pin6, LEDS2.pin12
  N38: IC3.pin7, LEDS2.pin11
  N39: IC3.pin8, LEDS2.pin10
  N40: IC3.pin9, LEDS2.pin9
  N41: IC3.pin11, J3.pin8
  N42: IC3.pin12, J3.pin7
  N43: IC3.pin13, J3.pin6
  N44: IC3.pin14, J3.pin5
  N45: IC3.pin15, J3.pin4
  N46: IC3.pin16, J3.pin3
  N47: IC3.pin17, J3.pin2
  N48: IC3.pin18, J3.pin1
  N49: IC4.pin2, LEDS3.pin16
  N50: IC4.pin3, LEDS3.pin15
  N51: IC4.pin4, LEDS3.pin14
  N52: IC4.pin5, LEDS3.pin13
  N53: IC4.pin6, LEDS3.pin12
  N54: IC4.pin7, LEDS3.pin11
  N55: IC4.pin8, LEDS3.pin10
  N56: IC4.pin9, LEDS3.pin9
  N57: IC4.pin11, J4.pin8
  N58: IC4.pin12, J4.pin7
  N59: IC4.pin13, J4.pin6
  N60: IC4.pin14, J4.pin5
  N61: IC4.pin15, J4.pin4
  N62: IC4.pin16, J4.pin3
  N63: IC4.pin17, J4.pin2
  N64: IC4.pin18, J4.pin1
  N65: LEDS.pin1, R1.Pin_1
  N66: LEDS.pin2, R2.Pin_1
  N67: LEDS.pin3, R3.Pin_1
  N68: LEDS.pin4, R4.Pin_1
  N69: LEDS.pin5, R5.Pin_1
  N70: LEDS.pin6, R6.Pin_1
  N71: LEDS.pin7, R7.Pin_1
  N72: LEDS.pin8, R8.Pin_1
  N73: R1.Pin_0, R2.Pin_0, R3.Pin_0, R4.Pin_0, R5.Pin_0, R6.Pin_0, R7.Pin_0, R8.Pin_0, R9.Pin_0, R10.Pin_0, R11.Pin_0, R12.Pin_0, R13.Pin_0, R14.Pin_0, R15.Pin_0, R16.Pin_0, R17.Pin_0, R18.Pin_0, R19.Pin_0, R20.Pin_0, R21.Pin_0, R22.Pin_0, R23.Pin_0, R24.Pin_0, R25.Pin_0, R26.Pin_0, R27.Pin_0, R28.Pin_0, R29.Pin_0, R30.Pin_0, R31.Pin_0, R32.Pin_0
  N74: LEDS1.pin1, R15.Pin_1
  N75: LEDS1.pin2, R16.Pin_1
  N76: LEDS1.pin3, R10.Pin_1
  N77: LEDS1.pin4, R11.Pin_1
  N78: LEDS1.pin5, R9.Pin_1
  N79: LEDS1.pin6, R12.Pin_1
  N80: LEDS1.pin7, R14.Pin_1
  N81: LEDS1.pin8, R13.Pin_1
  N82: LEDS2.pin1, R22.Pin_1
  N83: LEDS2.pin2, R20.Pin_1
  N84: LEDS2.pin3, R21.Pin_1
  N85: LEDS2.pin4, R18.Pin_1
  N86: LEDS2.pin5, R19.Pin_1
  N87: LEDS2.pin6, R17.Pin_1
  N88: LEDS2.pin7, R24.Pin_1
  N89: LEDS2.pin8, R23.Pin_1
  N90: LEDS3.pin1, R29.Pin_1
  N91: LEDS3.pin2, R30.Pin_1
  N92: LEDS3.pin3, R31.Pin_1
  N93: LEDS3.pin4, R26.Pin_1
  N94: LEDS3.pin5, R28.Pin_1
  N95: LEDS3.pin6, R32.Pin_1
  N96: LEDS3.pin7, R25.Pin_1
  N97: LEDS3.pin8, R27.Pin_1
